# Fritzing sketch Rendi - Alat Uji Emisi Kendaraan Motor Bakar Menggunakan Module Sensor Mq Series (saved by Fritzing 0.9.3b)

parts:
  A1 = DORHEA ESP32 GPIO breakout board 30pin
  M1 = DOIT Esp32 DevKit v1 (30 pins long, 11 pins width) [part_number=ESP32S-PIN30]  # not connected
  IC1 = MQ-2 [package="DIP (Dual Inline) [THT]"]
  Part1 = MQ-7 breakout
  Sensor1 = Gas Sensor Breakout Board
  Part2 = LCD1602-I2C

nets:
  N1: A1.Pin_4, A1.Pin_43, IC1.pin4
  N2: A1.Pin_6, A1.Pin_45, Part1.AO
  N3: A1.Pin_7, Sensor1.AOUT
  GND: A1.Pin_27, A1.Pin_57, A1.Pin_81, A1.Pin_85, IC1.pin2, Part1.GND, Sensor1.GND, Part2.GND
  VCC: A1.Pin_86, IC1.pin1, Part1.VCC, Sensor1.5V, Part2.VCC
  N4: A1.Pin_87, A1.Pin_123, Part2.SDA
  N5: A1.Pin_88, A1.Pin_126, Part2.SCL

custom parts:
  DORHEA ESP32 GPIO breakout board 30pin: ESP32 shield 30P expansion board, supports two power supply : DC 6.5-16v and USB 5.V
  DOIT Esp32 DevKit v1 (30 pins long, 11 pins width): The DOIT Esp32 DevKit v1 is one of the development board created by DOIT to evaluate the ESP-WROOM-32 module. It is based on the ESP32 microcontroller that boasts Wifi, Bluetooth, Ethernet and Low Power support all in a single chip. (vanepp) made breadboard work, adjusted pin numbering and labels and reduced size of schematic and cleaned up pcb. This chip is 30pins long (2 x15) and 11 pins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
  MQ-2: MQ-2 Gas Sensor module
  MQ-7 breakout: SKU: 101282
  Gas Sensor Breakout Board: Gas sensor breakout board. Input voltage is 5V. Sensor output is available in analog and digital.
  LCD1602-I2C: A standard character display, usually with 2x16 characters. Comes in many colors with LCM1602 IIC attached.
